# Fritzing sketch not-gates (saved by Fritzing 0.9.4)
breadboards: 1

parts:
  U1 = 4001 4 x 2 Input NOR Gate [part_number=4001 package="DIP (Dual Inline) [THT]"]
  part = 4001_4_x_2_input_NOR_gate_multipart_subpart1 [part_number=4001]  # not connected
  U1_1 = 4001_4_x_2_input_NOR_gate_multipart_subpart2 [part_number=4001]  # not connected
  U1_2 = 4001_4_x_2_input_NOR_gate_multipart_subpart3 [part_number=4001]  # not connected
  U1_3 = 4001_4_x_2_input_NOR_gate_multipart_subpart4 [part_number=4001]  # not connected
  U1_4 = 4001_4_x_2_input_NOR_gate_multipart_subpart5 [part_number=4001]  # not connected
  LED1 = LED - 5mm [color="Red (633nm)" package="5 mm [THT]"]
  VCC1 = Battery
  U2 = 4001 4 x 2 Input NOR Gate, single part [part_number=4001 package="DIP (Dual Inline) [THT]"]

nets:
  N1: U1.connector0, U1.connector1, U1.connector10
  N2: U1.connector2, U1.connector4, U1.connector5
  N3: U1.connector3, LED1.anode
  N4: U1.connector6, LED1.cathode, VCC1.-, U2.GND
  N5: U1.connector7, U1.connector8, U2.Q4
  N6: U1.connector9, U1.connector11, U1.connector12
  N7: U1.connector13, VCC1.+, U2.A3, U2.B3, U2.VDD
  N8: U2.Q3, U2.A4, U2.B4
