// Logisim project 4bit-adder-subtractor.circ as structural Verilog: 1 circuit, main circuit main
module main (
  input  C_in,
  input  B_0,
  input  A_0,
  input  B_1,
  input  A_1,
  input  B_2,
  input  A_2,
  input  B_3,
  input  A_3,
  output F_0,
  output F_1,
  output F_2,
  output F_3,
  output C_out
);

  wire and_1_out, and_2_out, and_3_out, and_4_out, and_5_out, and_6_out, and_7_out, and_8_out, or_1_out,
       or_2_out, or_3_out, xor_1_out, xor_2_out, xor_3_out, xor_4_out, xor_5_out, xor_6_out, xor_7_out,
       xor_8_out;

  xor xor_1 (xor_1_out, C_in, B_0);
  xor xor_2 (xor_2_out, C_in, B_1);
  xor xor_3 (xor_3_out, C_in, B_2);
  xor xor_4 (xor_4_out, C_in, B_3);
  xor xor_5 (xor_5_out, C_in, xor_1_out);
  xor xor_6 (xor_6_out, or_1_out, xor_2_out);
  xor xor_7 (xor_7_out, or_2_out, xor_3_out);
  xor xor_8 (xor_8_out, or_3_out, xor_4_out);
  xor xor_9 (F_0, xor_5_out, A_0);
  and and_1 (and_1_out, A_0, xor_5_out);
  and and_2 (and_2_out, C_in, xor_1_out);
  xor xor_10 (F_1, xor_6_out, A_1);
  and and_3 (and_3_out, A_1, xor_6_out);
  and and_4 (and_4_out, or_1_out, xor_2_out);
  xor xor_11 (F_2, xor_7_out, A_2);
  and and_5 (and_5_out, A_2, xor_7_out);
  and and_6 (and_6_out, or_2_out, xor_3_out);
  xor xor_12 (F_3, xor_8_out, A_3);
  and and_7 (and_7_out, A_3, xor_8_out);
  and and_8 (and_8_out, or_3_out, xor_4_out);
  or or_1 (or_1_out, and_1_out, and_2_out);
  or or_2 (or_2_out, and_3_out, and_4_out);
  or or_3 (or_3_out, and_5_out, and_6_out);
  or or_4 (C_out, and_7_out, and_8_out);
endmodule
